# Fritzing sketch simple scale connections (saved by Fritzing 0.9.3b)

parts:
  Bauteil1 = Arduino Nano (Rev3.0)
  S1 = Pushbutton [package="[THT]"]
  S2 = Toggle Switch [package=THT]
  R1 = Resistor [tolerance=±5% resistance=100k package=THT]
  U1 = LIPO-1000mAh [package=lipo-1000]
  D1 = Rectifier Diode [part_number=1N4001 package="300 mil [THT]"]
  Bauteil2 = HX711 Weighing Sensor Module
  Squix1 = OLED 0.96" 128x64 I2C SSD1306
  R2 = Resistor [tolerance=±5% resistance=10k package="2010 [SMD]"]

nets:
  GND: Bauteil1.GND, S1.Pin_3, S1.Pin_4, U1.-, Bauteil2.GND, R2.Pin_0
  N1: Bauteil1.D2, S1.Pin_1, S1.Pin_2
  N2: Bauteil1.VIN, S2.COM, R1.Pin_1, D1.cathode
  5V: Bauteil1.5V, D1.anode, Bauteil2.VCC
  N3: Bauteil1.A6, R1.Pin_0, R2.Pin_1
  N4: Bauteil1.A5, Squix1.SCL
  N5: Bauteil1.A4, Squix1.SCA
  N6: Bauteil1.A2, Bauteil2.CK/TX
  N7: Bauteil1.A1, Bauteil2.DO/RX
  3V3: Bauteil1.3V3, Squix1.VCC
  N8: Bauteil1.D13/SCK, Squix1.GND
  N9: S2.L1, U1.+

notes:
  1kg load cell
  protected (!) lithium battery
